# Fritzing sketch zisterne01 (saved by Fritzing 0.9.3b)
breadboards: 1

parts:
  U1 = ESP32S-HiLetgo [part_number=ESP32S-HiLetgo]
  hc-sr1 = hc-sr04

nets:
  N1: U1.GPIO9, hc-sr1.GND
  VIN: U1.VIN, hc-sr1.VCC
  N2: U1.GPIO22, hc-sr1.Trig
  N3: U1.GPIO23, hc-sr1.Echo

custom parts:
  ESP32S-HiLetgo: HiLetgo ESP-WROOM-32 ESP32 ESP-32S Development Board 2.4GHz Dual-Mode WiFi + Bluetooth Dual Cores Microcontroller The ESP32 integrated with Antenna switches, RF Balun, power amplifiers, low-noise amplifiers, filters, and management modules, and the entire solution occupies the least area of PCB. 2.4 GHz Wi-Fi plus Bluetooth dual-mode chip, with TSMC Ultra-low power consumption 40nm technology,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
